# Fritzing sketch EsquemaLigacao (saved by Fritzing 0.8.3b)

parts:
  Componente1 = Arduino Mega 2560 (Rev3)
  Componente2 = Arduino GPS Shield

nets:
  N1: Componente1.D19/RX1, Componente2.D_RX
  N2: Componente1.3V3, Componente2.3.3VIN
  N3: Componente1.5V, Componente2.5VIN
  GND: Componente1.GND, Componente2.GND
